// Logisim project ex2.circ as structural Verilog: 1 circuit, main circuit compute_BrUn
module compute_BrUn (
  input  [31:0] INSTRUCTION,
  output BrUn
);

  Comparator #(.mode("unsigned"), .width(2)) comparator_1 (
    .a(2'b11), .b(INSTRUCTION[14:13]), .eq(BrUn));  // open: gt, lt
endmodule
