// Logisim project partial-store.circ as structural Verilog: 1 circuit, main circuit partial_store
module partial_store (
  input  [31:0] Instruction,
  input  [31:0] MemAddress,
  input  [31:0] DataFromReg,
  input  MemWEn,
  output [3:0] MemWriteMask,
  output [31:0] DataToMem
);

  wire [3:0] multiplexer_2_out;
  wire [31:0] sb00, sh00;

  assign sb00 = {{24{1'b0}}, DataFromReg[7:0]};  // Bit_Extender bit_extender_1
  assign sh00 = {{16{1'b0}}, DataFromReg[15:0]};  // Bit_Extender bit_extender_2
  Multiplexer #(.width(4)) multiplexer_1 (.in0(4'b0000), .in1(multiplexer_2_out), .out(MemWriteMask), .sel(MemWEn));
  Multiplexer #(.select(4), .width(4)) multiplexer_2 (
    .in0(4'b0001), .in1(4'b0010), .in2(4'b0100), .in3(4'b1000), .in4(4'b0011), .in6(4'b1100), .in8(4'b1111),
    .out(multiplexer_2_out), .sel({Instruction[13:12], MemAddress[1:0]}));  // open: in5, in7, in9, in10, in11, in12, in13, in14, in15
  Multiplexer #(.select(4), .width(32)) multiplexer_3 (
    .in0(sb00), .in1({{16{1'b0}}, DataFromReg[7:0], {8{1'b0}}}),
    .in2({{8{1'b0}}, DataFromReg[7:0], {16{1'b0}}}), .in3({DataFromReg[7:0], {24{1'b0}}}), .in4(sh00),
    .in6({DataFromReg[15:0], {16{1'b0}}}), .in8(DataFromReg), .out(DataToMem),
    .sel({Instruction[13:12], MemAddress[1:0]}));  // open: in5, in7, in9, in10, in11, in12, in13, in14, in15

  // Other names for the same wires on the sheet: DataSel[3:0] = {Instruction[13:12], MemAddress[1:0]};
  //   offset[1:0] = MemAddress[1:0]; funct3[1:0] = Instruction[13:12]; sb01[15:8] = DataFromReg[7:0];
  //   sb10[23:16] = DataFromReg[7:0]; sb11[31:24] = DataFromReg[7:0]; sh10[31:16] = DataFromReg[15:0];
  //   sw00[31:0] = DataFromReg

  // Notes on the sheet:
  //   INPUTS to your circuit
  //   DON'T CHANGE THE LOCATIONS OF THE INPUTS AND OUTPUTS!
  //   OUTPUT from your circuit
endmodule
